# Fritzing sketch Untitled Sketch (saved by Fritzing 0.9.3b)
breadboards: 1

parts:
  Componente1 = Arduino Mega 2560 (Rev3)
  Componente2 = LCD1602-I2C
  S1 = H-Bridge with L298N
  M1 = DC Motor  # not connected
  M2 = DC Motor  # not connected
  M3 = DC Motor
  M4 = DC Motor  # not connected
  M5 = fc-51 [package=THT]
  SERVO1 = Tower Pro SG90 servo [part_number=101246]
  SERVO2 = Tower Pro SG90 servo [part_number=101246]
  M6 = fc-51 [package=THT]
  M7 = fc-51 [package=THT]
  M8 = fc-51 [package=THT]
  S3 = H-Bridge with L298N
  R1 = Resistor [tolerance=±5% resistance=220 package=THT]
  LED1 = LED - 5mm [color="Red (633nm)" package="5 mm [THT]"]
  LED2 = LED - 5mm [color="Blue (505nm)" package="5 mm [THT]"]
  R2 = Resistor [tolerance=±5% resistance=220 package=THT]
  LED3 = LED - 5mm [color="Yellow (592nm)" package="5 mm [THT]"]
  R3 = Resistor [tolerance=±5% resistance=220 package=THT]
  LED4 = LED - 5mm [color="Green (565nm)" package="5 mm [THT]"]
  R4 = Resistor [tolerance=±5% resistance=220 package=THT]
  S4 = Pushbutton [package="[THT]"]
  S5 = Pushbutton [package="[THT]"]
  R5 = Resistor [tolerance=±5% resistance=220 package=THT]
  R6 = Resistor [tolerance=±5% resistance=220 package=THT]
  S6 = Toggle Switch [package=THT]
  R7 = Resistor [tolerance=±5% resistance=220 package=THT]

nets:
  N1: Componente1.D21/SCL, Componente2.SCL
  N2: Componente1.D20/SDA, Componente2.SDA
  N3: Componente1.GND, M5.pin2, M6.pin2, M7.pin2, M8.pin2
  N4: Componente1.VIN, M5.pin3, M6.pin3, M7.pin3, M8.pin3
  N5: Componente1.D22, S1.IN1
  N6: Componente1.D23, S1.IN2
  N7: Componente1.D24, S3.IN1
  N8: Componente1.D25, S3.IN2
  N9: Componente1.D26, S1.IN3
  N10: Componente1.D27, S1.IN4
  N11: Componente1.D28, S3.IN3
  N12: Componente1.D29, S3.IN4
  N13: Componente1.D34, SERVO2.Signal
  N14: Componente1.D36, SERVO1.Signal
  N15: Componente1.D50, S6.L1, R7.Pin_1
  GND: Componente2.GND, SERVO1.GND, SERVO2.GND, R1.Pin_1, R2.Pin_1, R3.Pin_1, R4.Pin_1, R5.Pin_1, R6.Pin_1, R7.Pin_0
  +5V: Componente2.VCC, SERVO1.+5V, SERVO2.+5V, S4.Pin_3, S4.Pin_4, S5.Pin_3, S5.Pin_4, S6.COM
  N16: M3.pin_2, S3.M2-01
  N17: R1.Pin_0, LED1.cathode
  N18: LED2.cathode, R2.Pin_0
  N19: LED3.cathode, R3.Pin_0
  N20: LED4.cathode, R4.Pin_0
  N21: S4.Pin_1, S4.Pin_2, R5.Pin_0
  N22: S5.Pin_1, S5.Pin_2, R6.Pin_0

notes:
  MOTOR 1
  MOTOR 2
  MOTOR 3
  MOTOR 4
  CILINDROA
  CILINDRO B
  S1
  S2
  S3
  S4
  FINAL DE CARRERA

custom parts:
  LCD1602-I2C: A standard character display, usually with 2x16 characters. Comes in many colors with LCM1602 IIC attached.
  H-Bridge with L298N: h-bridge
  Tower Pro SG90 servo: Original file by John De Cristofaro http://www.adafruit.com/products/1449 Adafruit Feedback Servo (Small) Edited by: e-radionica.com 28/9/2015

// code stored in the sketch: Untitled.ino

#define PIN_MOTOR_1_N1 22
#define PIN_MOTOR_1_N2 23


#define MOTOR_1_STOP digitalWrite(PIN_MOTOR_1_N1,LOW);digitalWrite(PIN_MOTOR_1_N2,LOW)
#define MOTOR_1_FORWARD digitalWrite(PIN_MOTOR_1_N1,LOW);digitalWrite(PIN_MOTOR_1_N2,HIGH)
#define MOTOR_1_BACKWARD digitalWrite(PIN_MOTOR_1_N1,HIGH);digitalWrite(PIN_MOTOR_1_N2,LOW)

void setup() {
  pinMode(PIN_MOTOR_1_EN, OUTPUT);
  pinMode(PIN_MOTOR_1_N1, OUTPUT);
  pinMode(PIN_MOTOR_1_N2, OUTPUT);


}


void loop() {
 
  MOTOR_1_FORWARD;
  //MOTOR_2_FORWARD;
  delay(2000);
  MOTOR_1_BACKWARD;
  //MOTOR_2_BACKWARD;
  delay(2000);
}
